// Logisim project Aula 1.circ as structural Verilog: 2 circuits, main circuit main
module main (
  input  A,
  input  B,
  output C1,
  output S
);

  and and_1 (C1, A, B);
  xor xor_1 (S, A, B);
endmodule

module Cir6bits (
  input  in_1,
  input  in_2,
  input  in_3,
  input  in_4,
  input  in_5,
  input  in_6,
  output out_7,
  output out_8,
  output out_9
);

  wire main_6_c1;

  main main_1 ();  // open: C1, A, B, S
  main main_2 ();  // open: C1, A, B, S
  main main_3 ();  // open: C1, A, B, S
  main main_4 (.A(in_5), .B(in_6), .S(out_7));  // open: C1
  main main_5 (.A(in_3), .B(in_4), .S(out_8));  // open: C1
  main main_6 (.C1(main_6_c1), .A(in_1), .B(in_2), .S(out_9));
endmodule
