// Logisim project Circuito Sequencia.circ as structural Verilog: 1 circuit, main circuit main
module main (
  input  R,
  input  E,
  input  S,
  output out_4,
  output out_5
);

  wire and_1_out, and_2_out;

  and and_1 (and_1_out, R, E);
  and and_2 (and_2_out, E, S);
  nor nor_1 (out_4, and_1_out, out_5);
  nor nor_2 (out_5, out_4, and_2_out);
endmodule
